# Fritzing sketch Carrinho Modelo_B com Ponte L298N (saved by Fritzing 0.9.3b)

parts:
  Componente1 = Arduino Uno (Rev3)
  S1 = H-Bridge with L298N
  M1 = DC Motor
  M2 = DC Motor
  HC-SR04_Sensor_1 = HC-SR04 Ultrasonic Distance Sensor
  J3 = Basic Servo

nets:
  N1: Componente1.D8, S1.IN1
  N2: Componente1.D9_PWM, S1.IN2
  N3: Componente1.D10_PWM/SS, S1.IN3
  N4: Componente1.D11_PWM/MOSI, S1.IN4
  N5: Componente1.D12/MISO, J3.pulse
  N6: Componente1.D13/SCK, J3.vcc
  GND: Componente1.GND, J3.gnd
  N7: Componente1.D4, HC-SR04_Sensor_1.GND
  N8: Componente1.D5_PWM, HC-SR04_Sensor_1.ECHO
  N9: Componente1.D6_PWM, HC-SR04_Sensor_1.TRIG
  N10: Componente1.D7, HC-SR04_Sensor_1.VCC
  N11: S1.M1-01, M2.pin_2
  N12: S1.M1-02, M2.pin_1
  N13: S1.M2-01, M1.pin_2
  N14: S1.M2-02, M1.pin_1

custom parts:
  H-Bridge with L298N: h-bridge
