# Fritzing sketch Carrinho com Ponte L293D (saved by Fritzing 0.9.3b)

parts:
  Componente1 = Arduino Uno (Rev3)  # not connected
  HC-SR04_Sensor_1 = HC-SR04 Ultrasonic Distance Sensor
  Componente2 = Adafruit Motor/Stepper/Servo Shield [part_number="Adafruit #1438"]
  M1 = DC Motor
  M2 = DC Motor
  J1 = Basic Servo

nets:
  VCC: HC-SR04_Sensor_1.VCC, Componente2.+5V, J1.vcc
  N1: HC-SR04_Sensor_1.TRIG, Componente2.AD1
  N2: HC-SR04_Sensor_1.ECHO, Componente2.AD0
  GND: HC-SR04_Sensor_1.GND, Componente2.GND, J1.gnd
  N3: Componente2.M2A, M1.pin_1
  N4: Componente2.M2B, M1.pin_2
  N5: Componente2.M1B, M2.pin_1
  N6: Componente2.M1A, M2.pin_2
  N7: Componente2.D10, J1.pulse

custom parts:
  Adafruit Motor/Stepper/Servo Shield: The original Adafruit Motorshield kit is one of our most beloved kits, which is why we decided to make something even better. We have upgraded the shield kit to make the bestest, easiest way to drive DC and Stepper motors. This shield will make quick work of your next robotics project! We kept the ability to drive up to 4 DC motors or 2 stepper motors, but added many improvements: Instead of a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
