# Fritzing sketch Carrinho_ODIR_Modelo_Desafio_com_Ponte_L298N (saved by Fritzing 0.9.3b)

parts:
  Componente1 = Arduino Uno (Rev3)
  S1 = H-Bridge with L298N
  M1 = DC Motor
  M2 = DC Motor
  HC-SR04_Sensor_1 = HC-SR04 Ultrasonic Distance Sensor
  VCC1 = Battery

nets:
  N1: Componente1.D10_PWM/SS, S1.IN3
  N2: Componente1.D11_PWM/MOSI, S1.IN4
  N3: Componente1.D2, HC-SR04_Sensor_1.TRIG
  N4: Componente1.D3_PWM, HC-SR04_Sensor_1.ECHO
  N5: Componente1.D5_PWM, S1.IN1
  N6: Componente1.D6_PWM, S1.IN2
  5V: Componente1.5V, HC-SR04_Sensor_1.VCC
  GND: Componente1.GND, S1.GND, HC-SR04_Sensor_1.GND, VCC1.-
  VIN: Componente1.VIN, S1.5V
  N7: S1.12V, VCC1.+
  N8: S1.M1-01, M2.pin_2
  N9: S1.M1-02, M2.pin_1
  N10: S1.M2-01, M1.pin_2
  N11: S1.M2-02, M1.pin_1

custom parts:
  H-Bridge with L298N: h-bridge
